// Logisim project 16_bit_ALU.circ as structural Verilog
module _16_bit_ALU (
  input  [15:0] A0___A15,
  input  [15:0] B0___B15,
  input  Cin,
  input  A_invert,
  input  B_invert,
  input  [1:0] Operation,
  output BLE,
  output [15:0] Result,
  output ZERO_FLAG,
  output Cout
);

  wire comparator_1_eq, comparator_1_lt, Ignore_this_out, main_1_cout, main_2_cout, main_3_cout;

  Comparator #(.width(16)) comparator_1 (
    .a(A0___A15), .b(B0___B15), .eq(comparator_1_eq), .lt(comparator_1_lt));  // open: gt
  or or_1 (BLE, comparator_1_eq, comparator_1_lt);
  _4_bit_alu__1__main main_1 (
    .A_invert(A_invert), .B_invert(B_invert), .A0(A0___A15[0]), .A1(A0___A15[1]), .A2(A0___A15[2]),
    .A3(A0___A15[3]), .B0(B0___B15[0]), .B1(B0___B15[1]), .B2(B0___B15[2]), .B3(B0___B15[3]), .Cin(Cin),
    .Operation(Operation), .S0(Result[0]), .S1(Result[1]), .S2(Result[2]), .S3(Result[3]), .Cout(main_1_cout));
  _4_bit_alu__1__main main_2 (
    .A_invert(A_invert), .B_invert(B_invert), .A0(A0___A15[4]), .A1(A0___A15[5]), .A2(A0___A15[6]),
    .A3(A0___A15[7]), .B0(B0___B15[4]), .B1(B0___B15[5]), .B2(B0___B15[6]), .B3(B0___B15[7]),
    .Cin(main_1_cout), .Operation(Operation), .S0(Result[4]), .S1(Result[5]), .S2(Result[6]), .S3(Result[7]),
    .Cout(main_2_cout));
  _4_bit_alu__1__main main_3 (
    .A_invert(A_invert), .B_invert(B_invert), .A0(A0___A15[8]), .A1(A0___A15[9]), .A2(A0___A15[10]),
    .A3(A0___A15[11]), .B0(B0___B15[8]), .B1(B0___B15[9]), .B2(B0___B15[10]), .B3(B0___B15[11]),
    .Cin(main_2_cout), .Operation(Operation), .S0(Result[8]), .S1(Result[9]), .S2(Result[10]),
    .S3(Result[11]), .Cout(main_3_cout));
  _4_bit_alu__1__main main_4 (
    .A_invert(A_invert), .B_invert(B_invert), .A0(A0___A15[12]), .A1(A0___A15[13]), .A2(A0___A15[14]),
    .A3(A0___A15[15]), .B0(B0___B15[12]), .B1(B0___B15[13]), .B2(B0___B15[14]), .B3(B0___B15[15]),
    .Cin(main_3_cout), .Operation(Operation), .S0(Result[12]), .S1(Result[13]), .S2(Result[14]),
    .S3(Result[15]), .Cout(Cout));
  not not_1 (ZERO_FLAG, Ignore_this_out);
  or Ignore_this (Ignore_this_out, Result[0], Result[1], Result[2], Result[3], Result[4], Result[5], Result[6], Result[7], Result[8], Result[9], Result[10], Result[11], Result[12], Result[13], Result[14], Result[15]);
endmodule
