// Logisim project CPU_main.circ as structural Verilog: 2 circuits, main circuit main
module main (
  input  [15:0] in_1
);

  wire and_1_out, and_2_out, Branch, clock_1_out, clock_2_out, JUmp, main_1_alusrc, main_1_call,
       main_1_control_type, main_1_live, main_1_load, main_1_memread, main_1_move, main_1_negative_check,
       main_1_regdst, main_1_regwrite, main_1_rtn, main_1_store, n16_bit_alu_1_ble, register_2_q;
  wire [1:0] main_1_aluop;
  wire [2:0] multiplexer_3_out, multiplexer_5_out;
  wire [11:0] adder_1_out, adder_2_out, bit_extender_1_out, multiplexer_1_out, multiplexer_2_out,
       multiplexer_4_out, multiplexer_6_out, multiplexer_9_out, negator_1_out, PC_q, register_1_q;
  wire [15:0] bit_extender_3_out, multiplexer_7_out, multiplexer_8_out, multiplexer_10_out,
       n16_bit_alu_1_result, ram_1_data, ram_2_data, register_file_1_data1, register_file_1_data2;

  Multiplexer #(.width(12)) multiplexer_1 (
    .in0(multiplexer_9_out), .in1(register_1_q), .out(multiplexer_1_out), .sel(main_1_rtn));  // open: en
  // Probe on multiplexer_1_out
  Clock clock_1 (.out(clock_1_out));
  // Probe on multiplexer_9_out
  and and_1 (and_1_out, clock_1_out, main_1_live);
  Register #(.width(12)) PC (.D(multiplexer_1_out), .Q(PC_q), .clk(and_1_out));  // open: en, clr
  // Probe on adder_1_out
  Adder #(.width(12)) adder_1 (.a(12'h1), .b(PC_q), .out(adder_1_out));  // open: cin, cout
  Register #(.width(12)) register_1 (.D(multiplexer_2_out), .Q(register_1_q), .clk(and_1_out));  // open: en, clr
  Multiplexer #(.width(12)) multiplexer_2 (
    .in1(adder_1_out), .out(multiplexer_2_out), .sel(main_1_call));  // open: in0, en
  // Probe on multiplexer_2_out
  RAM #(.addrWidth(12), .dataWidth(16)) ram_1 (
    .addr(PC_q), .data(ram_1_data), .sel(1'b1), .clk(and_1_out));  // open: ld, clr
  // Probe on ram_1_data[3:1]
  // Probe on ram_1_data[9:4]
  Adder #(.width(12)) adder_2 (.a(adder_1_out), .b(multiplexer_4_out), .out(adder_2_out));  // open: cin, cout
  Multiplexer #(.width(3)) multiplexer_3 (
    .in0(ram_1_data[3:1]), .in1(ram_1_data[9:7]), .out(multiplexer_3_out), .sel(main_1_control_type));  // open: en
  // Probe on adder_2_out
  // Probe on multiplexer_4_out
  Negator #(.width(12)) negator_1 (.in(bit_extender_1_out), .out(negator_1_out));
  Bit_Extender #(.in_width(16), .out_width(12)) bit_extender_1 (.in(bit_extender_3_out), .out(bit_extender_1_out));
  Bit_Extender #(.in_width(6)) bit_extender_2 (.in(ram_1_data[9:4]));  // open: out
  Multiplexer #(.width(12)) multiplexer_4 (
    .in0(bit_extender_1_out), .in1(negator_1_out), .out(multiplexer_4_out), .sel(main_1_negative_check));  // open: en
  // Probe on ram_1_data[6:4]
  // Probe on ram_1_data[9:7]
  // Probe on multiplexer_5_out
  Multiplexer #(.width(3)) multiplexer_5 (
    .in0(multiplexer_3_out), .in1(ram_1_data[6:4]), .out(multiplexer_5_out), .sel(main_1_regdst));  // open: en
  // Probe on multiplexer_10_out
  assign bit_extender_3_out = {{12{1'b0}}, ram_1_data[3:0]};  // Bit_Extender bit_extender_3
  ControlUnit_main main_1 (
    .Opcode(ram_1_data[15:12]), .RegWrite(main_1_regwrite), .Regdst(main_1_regdst), .AluSrc(main_1_alusrc),
    .MemRead(main_1_memread), .ALUop(main_1_aluop), .Branch(Branch), .Jump(JUmp), .Load(main_1_load),
    .Store(main_1_store), .live(main_1_live), .Control_type(main_1_control_type),
    .Negative_check(main_1_negative_check), .RTN(main_1_rtn), .Call(main_1_call), .Move(main_1_move));
  Register #(.width(1)) register_2 (.D(main_1_move), .Q(register_2_q), .clk(clock_2_out));  // open: en, clr
  Clock #(.highDuration(2)) clock_2 (.out(clock_2_out));
  // Probe on bit_extender_3_out
  and and_2 (and_2_out, Branch, n16_bit_alu_1_ble);
  Register_file register_file_1 (
    .Write(main_1_regwrite), .Write_Register(multiplexer_5_out), .Register_Data(multiplexer_10_out),
    .Clock(and_1_out), .Data1(register_file_1_data1), .Data2(register_file_1_data2), .reset(1'b0),
    .Read_Regisiter1(ram_1_data[6:4]), .Read_Regisiter2(ram_1_data[9:7]));
  Multiplexer #(.width(12)) multiplexer_6 (
    .in0(adder_1_out), .in1(adder_2_out), .out(multiplexer_6_out), .sel(and_2_out));  // open: en
  Multiplexer #(.width(16)) multiplexer_7 (
    .in0(register_file_1_data1), .in1(in_1), .out(multiplexer_7_out), .sel(register_2_q));  // open: en
  Multiplexer #(.width(16)) multiplexer_8 (
    .in0(register_file_1_data2), .in1(bit_extender_3_out), .out(multiplexer_8_out), .sel(main_1_alusrc));  // open: en
  Multiplexer #(.width(12)) multiplexer_9 (
    .in0(multiplexer_6_out), .in1(adder_2_out), .out(multiplexer_9_out), .sel(JUmp));  // open: en
  // Probe on multiplexer_7_out
  // Probe on n16_bit_alu_1_result
  _16_bit_ALU u_16_bit_alu_1 (
    .A0___A15(multiplexer_7_out), .B0___B15(multiplexer_8_out), .A_invert(1'b0), .B_invert(1'b0),
    .Operation(main_1_aluop), .Cin(1'b0), .Result(n16_bit_alu_1_result), .BLE(n16_bit_alu_1_ble));  // open: Cout, ZERO_FLAG
  // Probe on n16_bit_alu_1_result
  RAM #(.addrWidth(16), .dataWidth(16), .bus("separate")) ram_2 (
    .addr(multiplexer_7_out), .din(n16_bit_alu_1_result), .data(ram_2_data), .str(main_1_store), .sel(1'b1),
    .clk(and_1_out), .ld(main_1_load));  // open: clr
  Multiplexer #(.width(16)) multiplexer_10 (
    .in0(n16_bit_alu_1_result), .in1(ram_2_data), .out(multiplexer_10_out), .sel(main_1_memread));  // open: en
endmodule

// Register file
module Register_file (
  input  Write,
  input  [2:0] Read_Regisiter1,
  input  [2:0] Write_Register,
  input  [2:0] Read_Regisiter2,
  input  [15:0] Register_Data,
  input  reset,
  input  Clock,
  output [15:0] Data1,
  output [15:0] Data2
);

  wire and_1_out, and_2_out, and_3_out, and_4_out, and_5_out, and_6_out, and_7_out, and_8_out,
       decoder_1_out0, decoder_1_out1, decoder_1_out2, decoder_1_out3, decoder_1_out4, decoder_1_out5,
       decoder_1_out6, decoder_1_out7;
  wire [15:0] register_1_q, register_2_q, register_3_q, register_4_q, register_5_q, register_6_q,
       register_7_q, register_8_q;

  Decoder #(.select(3), .enable("false")) decoder_1 (
    .out0(decoder_1_out0), .out1(decoder_1_out1), .out2(decoder_1_out2), .out3(decoder_1_out3),
    .out4(decoder_1_out4), .out5(decoder_1_out5), .out6(decoder_1_out6), .out7(decoder_1_out7),
    .sel(Write_Register));
  and and_1 (and_1_out, Write, decoder_1_out0);
  and and_2 (and_2_out, Write, decoder_1_out1);
  and and_3 (and_3_out, Write, decoder_1_out2);
  and and_4 (and_4_out, Write, decoder_1_out3);
  and and_5 (and_5_out, Write, decoder_1_out4);
  and and_6 (and_6_out, Write, decoder_1_out5);
  and and_7 (and_7_out, Write, decoder_1_out6);
  and and_8 (and_8_out, Write, decoder_1_out7);
  Register #(.width(16)) register_1 (.D(Register_Data), .en(and_1_out), .Q(register_1_q), .clk(Clock), .clr(reset));
  Register #(.width(16)) register_2 (.D(Register_Data), .en(and_2_out), .Q(register_2_q), .clk(Clock), .clr(reset));
  Register #(.width(16)) register_3 (.D(Register_Data), .en(and_3_out), .Q(register_3_q), .clk(Clock), .clr(reset));
  Register #(.width(16)) register_4 (.D(Register_Data), .en(and_4_out), .Q(register_4_q), .clk(Clock), .clr(reset));
  Register #(.width(16)) register_5 (.D(Register_Data), .en(and_5_out), .Q(register_5_q), .clk(Clock), .clr(reset));
  Register #(.width(16)) register_6 (.D(Register_Data), .en(and_6_out), .Q(register_6_q), .clk(Clock), .clr(reset));
  Register #(.width(16)) register_7 (.D(Register_Data), .en(and_7_out), .Q(register_7_q), .clk(Clock), .clr(reset));
  Register #(.width(16)) register_8 (.D(Register_Data), .en(and_8_out), .Q(register_8_q), .clk(Clock), .clr(reset));
  Multiplexer #(.select(3), .width(16)) multiplexer_1 (
    .in0(register_1_q), .in1(register_2_q), .in2(register_3_q), .in3(register_4_q), .in4(register_5_q),
    .in5(register_6_q), .in6(register_7_q), .in7(register_8_q), .out(Data1), .sel(Read_Regisiter1));  // open: en
  Multiplexer #(.select(3), .width(16)) multiplexer_2 (
    .in0(register_1_q), .in1(register_2_q), .in2(register_3_q), .in3(register_4_q), .in4(register_5_q),
    .in5(register_6_q), .in6(register_7_q), .in7(register_8_q), .out(Data2), .sel(Read_Regisiter2));  // open: en
endmodule
