// Logisim project ControlUnit.circ as structural Verilog: 1 circuit, main circuit main
module main (
  input  [3:0] Opcode,
  output RegWrite,
  output Regdst,
  output AluSrc,
  output MemRead,
  output [1:0] ALUop,
  output Branch,
  output Jump,
  output Load,
  output Store,
  output live,
  output Control_type,
  output Negative_check,
  output RTN,
  output Call,
  output Move
);

  wire and_2_out, and_3_out, and_6_out, not_1_out, not_2_out, not_3_out, not_4_out, not_5_out, not_6_out,
       not_7_out, not_8_out, not_9_out, not_10_out, not_11_out, not_12_out, not_13_out, not_14_out,
       not_15_out;

  not not_1 (not_1_out, Opcode[1]);
  not not_2 (not_2_out, Opcode[2]);
  not not_3 (not_3_out, Opcode[3]);
  Write_Register_main main_1 (.Inout(Opcode), .out_2(RegWrite));
  RegDst_main main_2 (.in_1(Opcode), .out_2(Regdst));
  ALUsrc_main main_3 (.in_1(Opcode), .out_2(AluSrc));
  MemRead_main main_4 (.in_1(Opcode), .out_2(MemRead));
  ALUop_main main_5 (.in_1(Opcode), .out_2(ALUop));
  Branch_main main_6 (.in_1(Opcode), .out_2(Branch));
  jump_main main_7 (.in_1(Opcode), .out_2(Jump));
  Load_main main_8 (.in_1(Opcode), .out_2(Load));
  Store_main main_9 (.in_1(Opcode), .out_2(Store));
  not not_4 (not_4_out, Opcode[0]);
  not not_5 (not_5_out, Opcode[0]);
  not not_6 (not_6_out, Opcode[2]);
  not not_7 (not_7_out, Opcode[2]);
  not not_8 (not_8_out, Opcode[0]);
  not not_9 (not_9_out, Opcode[0]);
  not not_10 (not_10_out, Opcode[1]);
  not not_11 (not_11_out, Opcode[3]);
  and and_1 (Move, Opcode[0], not_1_out, not_2_out, not_3_out);
  not not_12 (not_12_out, Opcode[1]);
  and and_2 (and_2_out, not_5_out, Opcode[1], not_6_out, Opcode[3]);
  and and_3 (and_3_out, Opcode[0], Opcode[1], not_7_out, Opcode[3]);
  not not_13 (not_13_out, Opcode[0]);
  not not_14 (not_14_out, Opcode[1]);
  not not_15 (not_15_out, Opcode[2]);
  and and_4 (RTN, not_8_out, Opcode[1], Opcode[2], Opcode[3]);
  and and_5 (Call, not_9_out, not_10_out, Opcode[2], not_11_out);
  and and_6 (and_6_out, not_4_out, not_12_out, Opcode[2], Opcode[3]);
  or or_1 (Control_type, and_2_out, and_3_out);
  and and_7 (Negative_check, not_13_out, not_14_out, not_15_out, Opcode[3]);
  not not_16 (live, and_6_out);
endmodule
