// Logisim project Store.circ as structural Verilog: 1 circuit, main circuit main
module main (
  input  [3:0] in_1,
  output out_2
);

  wire not_1_out, not_2_out;

  not not_1 (not_1_out, in_1[0]);
  and and_1 (out_2, not_1_out, in_1[1], in_1[2], not_2_out);
  not not_2 (not_2_out, in_1[3]);
endmodule
