// Logisim project c3.circ as structural Verilog: 1 circuit, main circuit main
module main (
  input  A0,
  input  A1,
  input  A2,
  input  B0,
  input  B1,
  input  B2,
  input  Cin,
  output C3
);

  wire A0_B0_out, A1_B1_out, and_1_out, and_2_out, and_3_out, and_4_out, and_5_out, and_6_out, or_1_out,
       or_2_out;

  and and_1 (and_1_out, A2, B2);
  or or_1 (or_1_out, A2, B2);
  and and_2 (and_2_out, A1, B1);
  or or_2 (or_2_out, A2, B2);
  or A1_B1 (A1_B1_out, A1, B1);
  and and_3 (and_3_out, A0, B0);
  or A0_B0 (A0_B0_out, A0, B0);
  and and_4 (and_4_out, or_1_out, and_2_out);
  and and_5 (and_5_out, or_2_out, A1_B1_out, and_3_out);
  and and_6 (and_6_out, or_2_out, A1_B1_out, A0_B0_out, Cin);
  or or_3 (C3, and_1_out, and_4_out, and_5_out, and_6_out);

  // Notes on the sheet:
  //   A2+B2
endmodule
